// Logisim project control_4roms_v1.circ as structural Verilog: 1 circuit, main circuit main
module main (
  input  in_1,
  input  in_2,
  input  in_3,
  input  in_4,
  input  in_5,
  input  in_6,
  input  in_7,
  input  in_8,
  input  in_9,
  input  manual_halt,
  input  in_11,
  input  Zero,
  input  Carry,
  input  EQUAL,
  input  SPARE
);

  wire and_1_out, and_2_out, and_3_out, and_4_out, and_5_out, and_6_out, and_7_out, and_8_out, and_9_out,
       and_10_out, and_11_out, and_12_out, buffer_1_out, buffer_2_out, buffer_3_out, buffer_4_out,
       buffer_5_out, buffer_6_out, buffer_7_out, buffer_8_out, buffer_9_out, buffer_10_out, buffer_11_out,
       buffer_12_out, buffer_13_out, buffer_14_out, buffer_15_out, buffer_16_out, buffer_17_out,
       buffer_18_out, buffer_19_out, buffer_20_out, buffer_21_out, buffer_22_out, buffer_23_out,
       buffer_24_out, buffer_25_out, button_1_out, button_2_out, counter_2_carry, j_k_ff_1_q, not_1_out,
       not_2_out, not_3_out, not_4_out, not_5_out, not_6_out, not_7_out, or_1_out, or_2_out, or_3_out,
       or_4_out, or_14_out, xor_1_out;
  wire [3:0] counter_3_q, dipswitch_1_sw4;
  wire [7:0] CONTROL_ROM_data, controlled_buffer_1_out, counter_1_q, counter_2_q, register_1_q, register_2_q,
       register_3_q, register_4_q, register_5_q, register_6_q, register_7_q, rom_1_data, rom_2_data,
       rom_3_data;
  wire [9:1] or_12_out;

  Button button_1 (.out(button_1_out));
  LED led_1 (.in(button_1_out));
  LED led_2 (.in(CONTROL_ROM_data[1]));
  not not_1 (not_1_out, button_1_out);
  DipSwitch #(.number(4)) dipswitch_1 (
    .sw1(dipswitch_1_sw4[3]), .sw2(dipswitch_1_sw4[2]), .sw3(dipswitch_1_sw4[1]), .sw4(dipswitch_1_sw4[0]));
  LED led_3 (.in(button_2_out));
  Button button_2 (.out(button_2_out));
  Counter counter_1 (
    .clr(button_2_out), .load(buffer_3_out), .count(counter_2_carry), .clk(button_1_out),
    .D(controlled_buffer_1_out), .Q(counter_1_q));  // open: up, carry
  Counter #(.trigger("falling")) counter_2 (
    .clr(button_2_out), .load(buffer_5_out), .count(CONTROL_ROM_data[1]), .clk(button_1_out),
    .D(controlled_buffer_1_out), .carry(counter_2_carry), .Q(counter_2_q));  // open: up
  Counter #(.width(4), .max('hf)) counter_3 (
    .clr(button_2_out), .load(rom_1_data[0]), .clk(not_1_out), .D(dipswitch_1_sw4), .Q(counter_3_q));  // open: up, count, carry
  assign controlled_buffer_1_out = buffer_4_out ? counter_1_q : 8'bz;  // Controlled_Buffer controlled_buffer_1
  assign controlled_buffer_1_out = buffer_6_out ? counter_2_q : 8'bz;  // Controlled_Buffer controlled_buffer_2
  Register register_1 (
    .D(controlled_buffer_1_out), .en(rom_1_data[1]), .clk(button_1_out), .Q(register_1_q), .clr(button_2_out));
  LED led_4 (.in(counter_3_q[0]));
  LED led_5 (.in(counter_3_q[2]));
  LED led_6 (.in(counter_3_q[1]));
  LED led_7 (.in(buffer_1_out));
  LED led_8 (.in(buffer_2_out));
  buf buffer_1 (buffer_1_out, CONTROL_ROM_data[6]);
  buf buffer_2 (buffer_2_out, CONTROL_ROM_data[7]);
  LED led_9 (.in(counter_3_q[3]));
  LED led_10 (.in(buffer_4_out));
  LED led_11 (.in(buffer_3_out));
  buf buffer_3 (buffer_3_out, CONTROL_ROM_data[4]);
  buf buffer_4 (buffer_4_out, CONTROL_ROM_data[5]);
  ROM #(.addrWidth(13)) CONTROL_ROM (
    .addr({counter_3_q[0], counter_3_q[1], counter_3_q[2], or_12_out, manual_halt}), .data(CONTROL_ROM_data));
  not not_2 (not_2_out, register_1_q[7]);
  not not_3 (not_3_out, register_1_q[5]);
  and and_1 (and_1_out, not_2_out, not_3_out);
  and and_2 (and_2_out, register_1_q[6], and_1_out);
  LED led_12 (.in(and_2_out));
  LED led_13 (.in(buffer_5_out));
  LED led_14 (.in(buffer_6_out));
  buf buffer_5 (buffer_5_out, CONTROL_ROM_data[2]);
  buf buffer_6 (buffer_6_out, CONTROL_ROM_data[3]);
  xor xor_1 (xor_1_out, register_1_q[4], or_1_out);
  or or_1 (or_1_out, or_2_out, or_3_out);
  Register register_2 (
    .D(controlled_buffer_1_out), .en(buffer_8_out), .clk(button_1_out), .Q(register_2_q), .clr(button_2_out));
  not not_4 (not_4_out, and_3_out);
  and and_3 (and_3_out, xor_1_out, and_2_out);
  and and_4 (and_4_out, register_1_q[0], Zero);
  or or_2 (or_2_out, and_4_out, and_5_out);
  and and_5 (and_5_out, register_1_q[1], Carry);
  and and_6 (and_6_out, register_1_q[2], EQUAL);
  or or_3 (or_3_out, and_6_out, and_7_out);
  and and_7 (and_7_out, register_1_q[3], SPARE);
  LED led_15 (.in(buffer_7_out));
  LED led_16 (.in(buffer_8_out));
  buf buffer_7 (buffer_7_out, rom_1_data[7]);
  buf buffer_8 (buffer_8_out, rom_1_data[6]);
  Register register_3 (
    .D(controlled_buffer_1_out), .en(buffer_9_out), .clk(button_1_out), .Q(register_3_q), .clr(button_2_out));
  assign controlled_buffer_1_out = buffer_7_out ? register_2_q : 8'bz;  // Controlled_Buffer controlled_buffer_3
  ROM #(.addrWidth(13)) rom_1 (
    .addr({counter_3_q[0], counter_3_q[1], counter_3_q[2], or_12_out, manual_halt}), .data(rom_1_data));
  and and_8 (and_8_out, register_1_q[0], not_4_out);
  and and_9 (and_9_out, register_1_q[1], not_4_out);
  and and_10 (and_10_out, register_1_q[2], not_4_out);
  and and_11 (and_11_out, register_1_q[3], not_4_out);
  and and_12 (and_12_out, register_1_q[4], not_4_out);
  LED led_17 (.in(buffer_9_out));
  LED led_18 (.in(buffer_10_out));
  buf buffer_9 (buffer_9_out, rom_1_data[4]);
  buf buffer_10 (buffer_10_out, rom_1_data[5]);
  assign controlled_buffer_1_out = buffer_10_out ? register_3_q : 8'bz;  // Controlled_Buffer controlled_buffer_4
  LED led_19 (.in(buffer_11_out));
  buf buffer_11 (buffer_11_out, rom_1_data[3]);
  RAM #(.addrWidth(16)) ram_1 (
    .addr({register_4_q, register_5_q}), .we(rom_1_data[2]), .oe(buffer_11_out), .clk(or_4_out),
    .data(controlled_buffer_1_out));
  or or_4 (or_4_out, button_1_out, not_5_out);
  not not_5 (not_5_out, button_1_out);
  Register register_4 (
    .D(controlled_buffer_1_out), .en(buffer_13_out), .clk(button_1_out), .Q(register_4_q), .clr(button_2_out));
  LED led_20 (.in(rom_1_data[2]));
  ROM #(.addrWidth(13)) rom_2 (
    .addr({counter_3_q[0], counter_3_q[1], counter_3_q[2], or_12_out, manual_halt}), .data(rom_2_data));
  or or_5 (or_12_out[9], counter_3_q[3], in_1);
  LED led_21 (.in(buffer_13_out));
  LED led_22 (.in(buffer_12_out));
  buf buffer_12 (buffer_12_out, rom_2_data[7]);
  buf buffer_13 (buffer_13_out, rom_2_data[6]);
  or or_6 (or_12_out[8], and_8_out, in_2);
  or or_7 (or_12_out[7], and_9_out, in_3);
  Register register_5 (
    .D(controlled_buffer_1_out), .en(buffer_15_out), .clk(button_1_out), .Q(register_5_q), .clr(button_2_out));
  assign controlled_buffer_1_out = buffer_12_out ? register_4_q : 8'bz;  // Controlled_Buffer controlled_buffer_5
  or or_8 (or_12_out[6], and_10_out, in_4);
  or or_9 (or_12_out[5], and_11_out, in_5);
  LED led_23 (.in(buffer_15_out));
  LED led_24 (.in(buffer_14_out));
  buf buffer_14 (buffer_14_out, rom_2_data[5]);
  buf buffer_15 (buffer_15_out, rom_2_data[4]);
  or or_10 (or_12_out[3], register_1_q[5], in_7);
  or or_11 (or_12_out[4], and_12_out, in_6);
  assign controlled_buffer_1_out = buffer_14_out ? register_5_q : 8'bz;  // Controlled_Buffer controlled_buffer_6
  or or_12 (or_12_out[1], register_1_q[7], in_9);
  or or_13 (or_12_out[2], register_1_q[6], in_8);
  Register register_6 (
    .D(controlled_buffer_1_out), .en(buffer_17_out), .clk(button_1_out), .Q(register_6_q), .clr(button_2_out));
  LED led_25 (.in(buffer_16_out));
  LED led_26 (.in(buffer_17_out));
  buf buffer_16 (buffer_16_out, rom_2_data[3]);
  buf buffer_17 (buffer_17_out, rom_2_data[2]);
  Register register_7 (
    .D(controlled_buffer_1_out), .en(buffer_18_out), .clk(button_1_out), .Q(register_7_q), .clr(button_2_out));
  assign controlled_buffer_1_out = buffer_16_out ? register_6_q : 8'bz;  // Controlled_Buffer controlled_buffer_7
  LED led_27 (.in(buffer_18_out));
  LED led_28 (.in(buffer_19_out));
  buf buffer_18 (buffer_18_out, rom_2_data[0]);
  buf buffer_19 (buffer_19_out, rom_2_data[1]);
  assign controlled_buffer_1_out = buffer_19_out ? register_7_q : 8'bz;  // Controlled_Buffer controlled_buffer_8
  ROM #(.addrWidth(13)) rom_3 (
    .addr({counter_3_q[0], counter_3_q[1], counter_3_q[2], or_12_out, manual_halt}), .data(rom_3_data));
  LED led_29 (.in(buffer_20_out));
  buf buffer_20 (buffer_20_out, rom_3_data[7]);
  LED led_30 (.in(buffer_22_out));
  LED led_31 (.in(buffer_21_out));
  buf buffer_21 (buffer_21_out, rom_3_data[6]);
  buf buffer_22 (buffer_22_out, rom_3_data[5]);
  LED led_32 (.in(rom_3_data[0]));
  LED led_33 (.in(buffer_23_out));
  buf buffer_23 (buffer_23_out, rom_3_data[4]);
  LED led_34 (.in(buffer_24_out));
  buf buffer_24 (buffer_24_out, rom_3_data[3]);
  LED led_35 (.in(rom_3_data[1]));
  LED led_36 (.in(rom_3_data[2]));
  not not_6 (not_6_out, rom_3_data[1]);
  LED led_37 (.in(buffer_25_out));
  buf buffer_25 (buffer_25_out, or_14_out);
  or or_14 (or_14_out, CONTROL_ROM_data[0], in_11);
  J_K_Flip_Flop j_k_ff_1 (
    .J(rom_3_data[2]), .K(not_7_out), .clk(button_1_out), .Q(j_k_ff_1_q));  // open: Qn, preset, reset
  not not_7 (not_7_out, not_6_out);
  LED led_38 (.in(j_k_ff_1_q));

  // Notes on the sheet:
  //   clock
  //   IPC INC
  //   Resetr
  //   IPC (counter)
  //   OUT
  //   ALU
  //   IPC HIGH
  //   contents of CONTROL_ROM (hex, n*v repeats v):
  //   20 8 2 13*0 20 8 2 13*0 20 8 2 13*0 20 8 2 13*0 20 8 2 13*0 20 8 2 13*0 20 8 2 13*0 20 8 2 13*0 20 8
  //   2 13*0 20 8 2 13*0 20 8 2 13*0 20 8 2 13*0 20 8 2 13*0 20 8 2 13*0 20 8 2 13*0 20 8 2 13*0 20 8 2
  //   13*0 20 8 2 13*0 20 8 2 13*0 20 8 2 13*0 20 8 2 13*0 20 8 2 13*0 20 8 2 13*0 20 8 2 13*0 20 8 2 13*0
  //   20 8 2 13*0 20 8 2 13*0 20 8 2 13*0 20 8 2 13*0 20 8 2 13*0 20 8 2 13*0 20 8 2 13*0 20 8 2 13*0 20 8
  //   2 20 8 2 20 8 2 7*0 20 8 2 20 8 2 20 8 2 7*0 20 8 2 20 8 0 2 9*0 20 8 2 20 8 0 2 9*0 20 8 2 20 8 0 2
  //   9*0 20 8 2 20 8 0 2 9*0 20 8 2 20 8 40 2 9*0 20 8 2 13*0 20 8 2 13*0 20 8 2 13*0 20 8 2 13*0 20 8 2
  //   13*0 20 8 2 13*0 20 8 2 13*0 20 8 2 13*0 20 8 2 13*0 20 8 2 13*0 20 8 2 13*0 20 8 2 13*0 20 8 2 13*0
  //   20 8 2 13*0 20 8 2 13*0 20 8 2 13*0 20 8 2 13*0 20 8 2 13*0 20 8 2 13*0 20 8 2 13*0 20 8 2 13*0 20 8
  //   2 13*0 20 8 2 13*0 20 8 2 13*0 20 8 2 0 2 10 4 2 8*0 20 8 2 2 2 11*0 20 8 2 2 2 11*0 20 8 2 13*0 20
  //   8 2 2 2 11*0 20 8 2 13*0 20 8 2 13*0 20 8 2 13*0 20 8 2 13*0 20 8 2 13*0 20 8 2 13*0 20 8 2 13*0 20
  //   8 2 13*0 20 8 2 13*0 20 8 2 13*0 20 8 2 13*0 20 8 2 13*0 20 8 2 2 2 11*0 20 8 2 2 2 11*0 20 8 2 13*0
  //   20 8 2 2 2 11*0 20 8 2 13*0 20 8 2 13*0 20 8 2 13*0 20 8 2 13*0 20 8 2 13*0 20 8 2 13*0 20 8 2 13*0
  //   20 8 2 13*0 20 8 2 13*0 20 8 2 13*0 20 8 2 13*0 20 8 2 20 8 11*0 20 8 2 20 8 11*0 20 8 2 10 4 11*0
  //   20 8 2 13*0 20 8 2 10 4 11*0 20 8 2 13*0 20 8 2 13*0 20 8 2 13*0 20 8 2 13*0 20 8 2 13*0 20 8 2 13*0
  //   20 8 2 13*0 20 8 2 13*0 20 8 2 13*0 20 8 2 13*0 20 8 2 13*0 20 8 2 13*0 20 8 2 13*0 20 8 2 13*0 20 8
  //   2 13*0 20 8 2 13*0 20 8 2 13*0 20 8 2 13*0 20 8 2 13*0 20 8 2 13*0 20 8 2 13*0 20 8 2 13*0 20 8 2
  //   13*0 20 8 2 13*0 20 8 2 13*0 20 8 2 13*0 20 8 2 13*0 20 8 2 13*0 20 8 2 13*0 20 8 2 13*0 20 8 2 13*0
  //   20 8 2 13*0 20 8 2 13*0 20 8 2 13*0 20 8 2 13*0 20 8 2 13*0 20 8 2 13*0 20 8 2 13*0 20 8 2 13*0 20 8
  //   2 13*0 20 8 2 13*0 20 8 2 13*0 20 8 2 13*0 20 8 2 13*0 20 8 2 13*0 20 8 2 13*0 20 8 2 13*0 20 8 2
  //   13*0 20 8 2 13*0 20 8 2 13*0 20 8 2 13*0 20 8 2 13*0 20 8 2 13*0 20 8 2 13*0 20 8 2 13*0 20 8 2 13*0
  //   20 8 2 13*0 20 8 2 13*0 20 8 2 13*0 20 8 2 13*0 20 8 2 13*0 20 8 2 13*0 20 8 2 13*0 20 8 2 13*0 20 8
  //   2 13*0 20 8 2 13*0 20 8 2 13*0 20 8 2 13*0 20 8 2 13*0 20 8 2 13*0 20 8 2 13*0 20 8 2 13*0 20 8 2
  //   13*0 20 8 2 13*0 20 8 2 13*0 20 8 2 13*0 20 8 2 13*0 20 8 2 13*0 20 8 2 13*0 20 8 2 13*0 20 8 2 13*0
  //   20 8 2 13*0 20 8 2 13*0 20 8 2 13*0 20 8 2 13*0 20 8 2 13*0 20 8 2 13*0 20 8 2 13*0 20 8 2 13*0 20 8
  //   2 13*0 20 8 2 13*0 20 8 2 13*0 20 8 2 13*0 20 8 2 4 12*0 20 8 2 10 12*0 20 8 2 13*0 20 8 2 13*0 20 8
  //   2 13*0 20 8 2 13*0 20 8 2 40 12*0 20 8 2 13*0 20 8 2 13*0 20 8 2 4 12*0 20 8 2 10 12*0 20 8 2 13*0
  //   20 8 2 13*0 20 8 2 13*0 20 8 2 13*0 20 8 2 40 12*0 20 8 2 13*0 20 8 2 13*0 20 8 2 4 12*0 20 8 2 10
  //   12*0 20 8 2 13*0 20 8 2 13*0 20 8 2 13*0 20 8 2 13*0 20 8 2 40 12*0 20 8 2 8 12*0 20 8 2 20 12*0 20
  //   8 2 8 12*0 20 8 2 20 12*0 20 8 2 8 12*0 20 8 2 20 12*0 20 8 2 13*0 20 8 2 13*0 20 8 2 13*0 20 8 2
  //   13*0 20 8 2 13*0 20 8 2 13*0 20 8 2 13*0 20 8 2 13*0 20 8 2 13*0 20 8 2 13*0 20 8 2 13*0 20 8 2 13*0
  //   20 8 2 80 12*0 20 8 2 80 12*0 20 8 2 80 12*0 20 8 2 84 12*0 20 8 2 90 12*0 20 8 2 80 12*0 20 8 2 80
  //   12*0 20 8 2 80 12*0 20 8 2 80 12*0 20 8 2 c0 12*0 20 8 2 13*0 20 8 2 13*0 20 8 2 13*0 20 8 2 13*0 20
  //   8 2 13*0 20 8 2 13*0 20 8 2 13*0 20 8 2 13*0 20 8 2 1
  //   IPC LOW
  //   A
  //   contents of rom_1 (hex, n*v repeats v):
  //   0 0 a 13*1 0 0 a 1 0 11*1 0 0 a 1 0 11*1 0 0 a 1 0 11*1 0 0 a 1 0 11*1 0 0 a 13*1 0 0 a 13*1 0 0 a
  //   13*1 0 0 a 1 0 11*1 0 0 a 1 0 11*1 0 0 a 1 0 11*1 0 0 a 1 0 11*1 0 0 a 1 0 11*1 0 0 a 13*1 0 0 a
  //   13*1 0 0 a 13*1 0 0 a 13*1 0 0 a 13*1 0 0 a 13*1 0 0 a 13*1 0 0 a 13*1 0 0 a 13*1 0 0 a 13*1 0 0 a
  //   13*1 0 0 a 13*1 0 0 a 13*1 0 0 a 13*1 0 0 a 13*1 0 0 a 13*1 0 0 a 13*1 0 0 a 13*1 0 0 a 13*1 0 0 a
  //   13*1 0 0 a 0 0 8 0 0 8 4 0 85 4*1 0 0 a 0 0 8 0 0 8 4 0 49 4*1 0 0 a 0 0 48 10*1 0 0 a 0 0 18 10*1 0
  //   0 a 0 0 8 10*1 0 0 a 0 0 8 10*1 0 0 a 0 0 8 10*1 0 0 a 13*1 0 0 a 13*1 0 0 a 13*1 0 0 a 13*1 0 0 a
  //   13*1 0 0 a 13*1 0 0 a 13*1 0 0 a 13*1 0 0 a 13*1 0 0 a 13*1 0 0 a 13*1 0 0 a 13*1 0 0 a 13*1 0 0 a
  //   13*1 0 0 a 13*1 0 0 a 13*1 0 0 a 13*1 0 0 a 13*1 0 0 a 13*1 0 0 a 13*1 0 0 a 13*1 0 0 a 13*1 0 0 a
  //   13*1 0 0 a 13*1 0 0 a 0 0 8 0 0 8 7*1 0 0 a 0 12*1 0 0 a 0 12*1 0 0 a 13*1 0 0 a 0 12*1 0 0 a 13*1 0
  //   0 a 13*1 0 0 a 13*1 0 0 a 13*1 0 0 a 13*1 0 0 a 13*1 0 0 a 13*1 0 0 a 13*1 0 0 a 13*1 0 0 a 13*1 0 0
  //   a 13*1 0 0 a 13*1 0 0 a 0 12*1 0 0 a 0 12*1 0 0 a 13*1 0 0 a 0 12*1 0 0 a 13*1 0 0 a 13*1 0 0 a 13*1
  //   0 0 a 13*1 0 0 a 13*1 0 0 a 13*1 0 0 a 13*1 0 0 a 13*1 0 0 a 13*1 0 0 a 13*1 0 0 a 13*1 0 0 a 0 0
  //   11*1 0 0 a 0 0 11*1 0 0 a 0 0 11*1 0 0 a 0 0 11*1 0 0 a 0 0 11*1 0 0 a 0 0 11*1 0 0 a 13*1 0 0 a
  //   13*1 0 0 a 13*1 0 0 a 13*1 0 0 a 13*1 0 0 a 13*1 0 0 a 13*1 0 0 a 13*1 0 0 a 13*1 0 0 a 13*1 0 0 a
  //   13*1 0 0 a 13*1 0 0 a 13*1 0 0 a 13*1 0 0 a 13*1 0 0 a 13*1 0 0 a 13*1 0 0 a 13*1 0 0 a 13*1 0 0 a
  //   13*1 0 0 a 13*1 0 0 a 13*1 0 0 a 13*1 0 0 a 13*1 0 0 a 13*1 0 0 a 13*1 0 0 a 13*1 0 0 a 13*1 0 0 a
  //   13*1 0 0 a 13*1 0 0 a 13*1 0 0 a 13*1 0 0 a 13*1 0 0 a 13*1 0 0 a 13*1 0 0 a 13*1 0 0 a 13*1 0 0 a
  //   13*1 0 0 a 13*1 0 0 a 13*1 0 0 a 13*1 0 0 a 13*1 0 0 a 13*1 0 0 a 13*1 0 0 a 13*1 0 0 a 13*1 0 0 a
  //   13*1 0 0 a 13*1 0 0 a 13*1 0 0 a 13*1 0 0 a 13*1 0 0 a 13*1 0 0 a 13*1 0 0 a 13*1 0 0 a 13*1 0 0 a
  //   13*1 0 0 a 13*1 0 0 a 13*1 0 0 a 13*1 0 0 a 13*1 0 0 a 13*1 0 0 a 13*1 0 0 a 13*1 0 0 a 13*1 0 0 a
  //   13*1 0 0 a 13*1 0 0 a 13*1 0 0 a 13*1 0 0 a 13*1 0 0 a 13*1 0 0 a 13*1 0 0 a 13*1 0 0 a 13*1 0 0 a
  //   13*1 0 0 a 13*1 0 0 a 13*1 0 0 a 13*1 0 0 a 13*1 0 0 a 13*1 0 0 a 13*1 0 0 a 13*1 0 0 a 13*1 0 0 a
  //   13*1 0 0 a 13*1 0 0 a 13*1 0 0 a 13*1 0 0 a 13*1 0 0 a 13*1 0 0 a 13*1 0 0 a 13*1 0 0 a 91 12*1 0 0
  //   a 85 12*1 0 0 a 81 12*1 0 0 a 81 12*1 0 0 a 81 12*1 0 0 a 81 12*1 0 0 a 81 12*1 0 0 a 81 12*1 0 0 a
  //   81 12*1 0 0 a 61 12*1 0 0 a 25 12*1 0 0 a 21 12*1 0 0 a 21 12*1 0 0 a 21 12*1 0 0 a 21 12*1 0 0 a 21
  //   12*1 0 0 a 21 12*1 0 0 a 21 12*1 0 0 a 49 12*1 0 0 a 19 12*1 0 0 a 9 12*1 0 0 a 9 12*1 0 0 a 9 12*1
  //   0 0 a 9 12*1 0 0 a 9 12*1 0 0 a 9 12*1 0 0 a 9 12*1 0 0 a 41 12*1 0 0 a 41 12*1 0 0 a 11 12*1 0 0 a
  //   11 12*1 0 0 a 5 12*1 0 0 a 5 12*1 0 0 a 41 12*1 0 0 a 41 12*1 0 0 a 11 12*1 0 0 a 11 12*1 0 0 a 5
  //   12*1 0 0 a 5 12*1 0 0 a 41 12*1 0 0 a 41 12*1 0 0 a 11 12*1 0 0 a 11 12*1 0 0 a 5 12*1 0 0 a 5 12*1
  //   0 0 a 41 12*1 0 0 a 11 12*1 0 0 a 5 12*1 0 0 a 13*1 0 0 a 13*1 0 0 a 13*1 0 0 a 13*1 0 0 a 13*1 0 0
  //   a 13*1 0 0 a 13*1 0 0 a 13*1 0 0 a 13*1 0 0 a 13*1 0 0 a 13*1 0 0 a 13*1 0 0 a 13*1 0 0 a 13*1 0 0 a
  //   13*1 0 0 a 13*1
  //   B
  //   MEM
  //   contents of rom_2 (hex, n*v repeats v):
  //   8*8 3 28 6*8 7b 7*8 1b 7*8 7 7*8 28 7*8 28 7*8 48 7*8 4b 7*8 33 28 6*8 6f 7*8 37 7*8 43 167*8 89 10
  //   6a 71 f5 18 8 8 89 10 6a 71 bd 18 8 8 6a 69 bd 18 4*8 6a 69 dd 18 4*8 6a 69 9d 18 4*8 6a 69 9d 18
  //   4*8 6a 69 3d 18 196*8 9d 10 5e 51 4*8 9d 10 5e 51 5*8 10 5e 51 4*8 9d 10 5e 51 5*8 10 5e 51 4*8 9d
  //   10 5e 51 5*8 10 5e 51 204*8 69 6a 6*8 89 8a 6*8 4d 4e 6*8 8d 8e 6*8 51 52 6*8 71 72 726*8 d5 7*8 f5
  //   7*8 55 7*8 56 7*8 75 7*8 76 7*8 95 7*8 96 7*8 35 7*8 b9 7*8 f9 7*8 59 7*8 5a 7*8 79 7*8 7a 7*8 99
  //   7*8 9a 7*8 39 7*8 bd 7*8 dd 7*8 5d 7*8 5e 7*8 7d 7*8 7e 7*8 9d 7*8 9e 7*8 3d 7*8 a9 7*8 aa 7*8 c9
  //   7*8 ca 7*8 e9 7*8 ea 7*8 ad 7*8 ae 7*8 cd 7*8 ce 7*8 ed 7*8 ee 7*8 b1 7*8 b2 7*8 d1 7*8 d2 7*8 f1
  //   7*8 f2 7*8 a5 7*8 c5 7*8 e5 7*8 45 7*8 46 7*8 65 7*8 66 7*8 85 7*8 86 7*8 25 71*8 4 7*8
  //   MR_HIGH
  //   MR_LOW
  //   TR_HIGH
  //   TR_LOW
  //   contents of rom_3 (hex, n*v repeats v):
  //   19*0 5 15*0 79 15*0 61 15*0 81 15*0 4 15*0 2 15*0 3 15*0 49 15*0 35 15*0 d9 15*0 b1 15*0 9
  //   M
  //   S3
  //   ALU
  //   S2
  //   ALU WR
  //   S1
  //   S0
  //   set
  //   Clear
  //   HALT
  //   Carry IN
endmodule
