// Logisim project control_5roms_v1.circ as structural Verilog: 1 circuit, main circuit main
module main (
  input  in_1,
  input  in_2,
  input  in_3,
  input  in_4,
  input  in_5,
  input  in_6,
  input  in_7,
  input  in_8,
  input  in_9,
  input  manual_halt,
  input  in_11,
  input  Zero,
  input  Carry,
  input  EQUAL,
  input  SPARE
);

  wire and_1_out, and_2_out, and_3_out, and_4_out, and_5_out, and_6_out, and_7_out, and_8_out, and_9_out,
       and_10_out, and_11_out, and_12_out, buffer_1_out, buffer_2_out, buffer_3_out, buffer_4_out,
       buffer_5_out, buffer_6_out, buffer_7_out, buffer_8_out, buffer_9_out, buffer_10_out, buffer_11_out,
       buffer_12_out, buffer_13_out, buffer_14_out, buffer_15_out, buffer_16_out, buffer_17_out,
       buffer_18_out, buffer_19_out, buffer_20_out, buffer_21_out, buffer_22_out, buffer_23_out,
       buffer_24_out, buffer_25_out, buffer_26_out, buffer_27_out, buffer_28_out, buffer_29_out,
       buffer_30_out, button_1_out, button_2_out, counter_2_carry, j_k_ff_1_q, not_1_out, not_2_out,
       not_3_out, not_4_out, not_5_out, not_6_out, not_7_out, or_1_out, or_2_out, or_3_out, or_4_out,
       or_14_out, xor_1_out;
  wire [3:0] counter_3_q, dipswitch_1_sw4;
  wire [7:0] CONTROL_ROM_data, controlled_buffer_1_out, counter_1_q, counter_2_q, register_1_q, register_2_q,
       register_3_q, register_4_q, register_5_q, register_6_q, register_7_q, rom_1_data, rom_2_data,
       rom_3_data, rom_4_data;
  wire [11:3] or_5_out;

  Button button_1 (.out(button_1_out));
  LED led_1 (.in(button_1_out));
  LED led_2 (.in(CONTROL_ROM_data[7]));
  not not_1 (not_1_out, button_1_out);
  DipSwitch #(.number(4)) dipswitch_1 (
    .sw1(dipswitch_1_sw4[3]), .sw2(dipswitch_1_sw4[2]), .sw3(dipswitch_1_sw4[1]), .sw4(dipswitch_1_sw4[0]));
  LED led_3 (.in(button_2_out));
  Button button_2 (.out(button_2_out));
  Counter counter_1 (
    .clr(button_2_out), .load(buffer_2_out), .count(counter_2_carry), .clk(button_1_out),
    .D(controlled_buffer_1_out), .Q(counter_1_q));  // open: up, carry
  Counter #(.trigger("falling")) counter_2 (
    .clr(button_2_out), .load(buffer_5_out), .count(CONTROL_ROM_data[7]), .clk(button_1_out),
    .D(controlled_buffer_1_out), .carry(counter_2_carry), .Q(counter_2_q));  // open: up
  Counter #(.width(4), .max('hf)) counter_3 (
    .clr(button_2_out), .load(rom_1_data[0]), .clk(not_1_out), .D(dipswitch_1_sw4), .Q(counter_3_q));  // open: up, count, carry
  assign controlled_buffer_1_out = buffer_3_out ? counter_1_q : 8'bz;  // Controlled_Buffer controlled_buffer_1
  assign controlled_buffer_1_out = buffer_6_out ? counter_2_q : 8'bz;  // Controlled_Buffer controlled_buffer_2
  Register register_1 (
    .D(controlled_buffer_1_out), .en(rom_1_data[1]), .clk(button_1_out), .Q(register_1_q), .clr(button_2_out));
  LED led_4 (.in(counter_3_q[0]));
  LED led_5 (.in(counter_3_q[2]));
  LED led_6 (.in(counter_3_q[1]));
  LED led_7 (.in(buffer_1_out));
  buf buffer_1 (buffer_1_out, CONTROL_ROM_data[6]);
  LED led_8 (.in(counter_3_q[3]));
  LED led_9 (.in(buffer_3_out));
  LED led_10 (.in(buffer_2_out));
  buf buffer_2 (buffer_2_out, CONTROL_ROM_data[4]);
  buf buffer_3 (buffer_3_out, CONTROL_ROM_data[5]);
  buf buffer_4 (buffer_4_out, rom_1_data[1]);
  LED led_11 (.in(buffer_4_out));
  ROM #(.addrWidth(13)) CONTROL_ROM (.addr({manual_halt, or_5_out, counter_3_q[2:0]}), .data(CONTROL_ROM_data));
  not not_2 (not_2_out, register_1_q[7]);
  not not_3 (not_3_out, register_1_q[5]);
  and and_1 (and_1_out, not_2_out, not_3_out);
  and and_2 (and_2_out, register_1_q[6], and_1_out);
  LED led_12 (.in(and_2_out));
  LED led_13 (.in(buffer_5_out));
  LED led_14 (.in(buffer_6_out));
  buf buffer_5 (buffer_5_out, CONTROL_ROM_data[2]);
  buf buffer_6 (buffer_6_out, CONTROL_ROM_data[3]);
  xor xor_1 (xor_1_out, register_1_q[4], or_1_out);
  or or_1 (or_1_out, or_2_out, or_3_out);
  LED led_15 (.in(buffer_7_out));
  buf buffer_7 (buffer_7_out, CONTROL_ROM_data[1]);
  buf buffer_8 (buffer_8_out, CONTROL_ROM_data[0]);
  not not_4 (not_4_out, and_3_out);
  and and_3 (and_3_out, xor_1_out, and_2_out);
  and and_4 (and_4_out, register_1_q[0], Zero);
  or or_2 (or_2_out, and_4_out, and_5_out);
  and and_5 (and_5_out, register_1_q[1], Carry);
  and and_6 (and_6_out, register_1_q[2], EQUAL);
  or or_3 (or_3_out, and_6_out, and_7_out);
  and and_7 (and_7_out, register_1_q[3], SPARE);
  RAM #(.addrWidth(16)) ram_1 (
    .addr({register_4_q, register_5_q}), .we(buffer_8_out), .oe(buffer_7_out), .clk(or_4_out),
    .data(controlled_buffer_1_out));
  or or_4 (or_4_out, button_1_out, not_5_out);
  not not_5 (not_5_out, button_1_out);
  Register register_2 (
    .D(controlled_buffer_1_out), .en(buffer_10_out), .clk(button_1_out), .Q(register_2_q), .clr(button_2_out));
  LED led_16 (.in(buffer_8_out));
  LED led_17 (.in(buffer_10_out));
  LED led_18 (.in(buffer_9_out));
  buf buffer_9 (buffer_9_out, rom_1_data[7]);
  buf buffer_10 (buffer_10_out, rom_1_data[6]);
  ROM #(.addrWidth(13)) rom_1 (.addr({manual_halt, or_5_out, counter_3_q[2:0]}), .data(rom_1_data));
  and and_8 (and_8_out, register_1_q[0], not_4_out);
  and and_9 (and_9_out, register_1_q[1], not_4_out);
  and and_10 (and_10_out, register_1_q[2], not_4_out);
  and and_11 (and_11_out, register_1_q[3], not_4_out);
  and and_12 (and_12_out, register_1_q[4], not_4_out);
  Register register_3 (
    .D(controlled_buffer_1_out), .en(buffer_13_out), .clk(button_1_out), .Q(register_3_q), .clr(button_2_out));
  assign controlled_buffer_1_out = buffer_9_out ? register_2_q : 8'bz;  // Controlled_Buffer controlled_buffer_3
  LED led_19 (.in(buffer_11_out));
  buf buffer_11 (buffer_11_out, rom_1_data[0]);
  LED led_20 (.in(buffer_12_out));
  LED led_21 (.in(buffer_13_out));
  buf buffer_12 (buffer_12_out, rom_1_data[5]);
  buf buffer_13 (buffer_13_out, rom_1_data[4]);
  Register register_4 (
    .D(controlled_buffer_1_out), .en(buffer_15_out), .clk(button_1_out), .Q(register_4_q), .clr(button_2_out));
  assign controlled_buffer_1_out = buffer_12_out ? register_3_q : 8'bz;  // Controlled_Buffer controlled_buffer_4
  ROM #(.addrWidth(13)) rom_2 (.addr({manual_halt, or_5_out, counter_3_q[2:0]}), .data(rom_2_data));
  or or_5 (or_5_out[3], counter_3_q[3], in_1);
  LED led_22 (.in(buffer_15_out));
  LED led_23 (.in(buffer_14_out));
  buf buffer_14 (buffer_14_out, rom_2_data[7]);
  buf buffer_15 (buffer_15_out, rom_2_data[6]);
  or or_6 (or_5_out[4], and_8_out, in_2);
  or or_7 (or_5_out[5], and_9_out, in_3);
  Register register_5 (
    .D(controlled_buffer_1_out), .en(buffer_17_out), .clk(button_1_out), .Q(register_5_q), .clr(button_2_out));
  assign controlled_buffer_1_out = buffer_14_out ? register_4_q : 8'bz;  // Controlled_Buffer controlled_buffer_5
  or or_8 (or_5_out[6], and_10_out, in_4);
  or or_9 (or_5_out[7], and_11_out, in_5);
  LED led_24 (.in(buffer_17_out));
  LED led_25 (.in(buffer_16_out));
  buf buffer_16 (buffer_16_out, rom_2_data[5]);
  buf buffer_17 (buffer_17_out, rom_2_data[4]);
  or or_10 (or_5_out[9], register_1_q[5], in_7);
  or or_11 (or_5_out[8], and_12_out, in_6);
  assign controlled_buffer_1_out = buffer_16_out ? register_5_q : 8'bz;  // Controlled_Buffer controlled_buffer_6
  or or_12 (or_5_out[11], register_1_q[7], in_9);
  or or_13 (or_5_out[10], register_1_q[6], in_8);
  Register register_6 (
    .D(controlled_buffer_1_out), .en(buffer_19_out), .clk(button_1_out), .Q(register_6_q), .clr(button_2_out));
  LED led_26 (.in(buffer_18_out));
  LED led_27 (.in(buffer_19_out));
  buf buffer_18 (buffer_18_out, rom_2_data[3]);
  buf buffer_19 (buffer_19_out, rom_2_data[2]);
  Register register_7 (
    .D(controlled_buffer_1_out), .en(buffer_20_out), .clk(button_1_out), .Q(register_7_q), .clr(button_2_out));
  assign controlled_buffer_1_out = buffer_18_out ? register_6_q : 8'bz;  // Controlled_Buffer controlled_buffer_7
  LED led_28 (.in(buffer_20_out));
  LED led_29 (.in(buffer_21_out));
  buf buffer_20 (buffer_20_out, rom_2_data[0]);
  buf buffer_21 (buffer_21_out, rom_2_data[1]);
  assign controlled_buffer_1_out = buffer_21_out ? register_7_q : 8'bz;  // Controlled_Buffer controlled_buffer_8
  ROM #(.addrWidth(13)) rom_3 (.addr({manual_halt, or_5_out, counter_3_q[2:0]}), .data(rom_3_data));
  LED led_30 (.in(buffer_23_out));
  LED led_31 (.in(buffer_22_out));
  LED led_32 (.in(buffer_24_out));
  buf buffer_22 (buffer_22_out, controlled_buffer_1_out[2]);
  buf buffer_23 (buffer_23_out, controlled_buffer_1_out[4]);
  buf buffer_24 (buffer_24_out, controlled_buffer_1_out[3]);
  LED led_33 (.in(buffer_26_out));
  LED led_34 (.in(buffer_25_out));
  buf buffer_25 (buffer_25_out, controlled_buffer_1_out[0]);
  buf buffer_26 (buffer_26_out, controlled_buffer_1_out[1]);
  assign controlled_buffer_1_out = rom_4_data[2] ? rom_3_data : 8'bz;  // Controlled_Buffer controlled_buffer_9
  ROM #(.addrWidth(13)) rom_4 (.addr({manual_halt, or_5_out, counter_3_q[2:0]}), .data(rom_4_data));
  LED led_35 (.in(buffer_27_out));
  buf buffer_27 (buffer_27_out, rom_4_data[7]);
  LED led_36 (.in(buffer_28_out));
  buf buffer_28 (buffer_28_out, rom_4_data[2]);
  LED led_37 (.in(buffer_29_out));
  LED led_38 (.in(rom_4_data[5]));
  buf buffer_29 (buffer_29_out, rom_4_data[6]);
  not not_6 (not_6_out, not_7_out);
  LED led_39 (.in(rom_4_data[4]));
  not not_7 (not_7_out, rom_4_data[4]);
  LED led_40 (.in(j_k_ff_1_q));
  J_K_Flip_Flop j_k_ff_1 (
    .J(rom_4_data[5]), .K(not_6_out), .clk(button_1_out), .Q(j_k_ff_1_q));  // open: Qn, preset, reset
  LED led_41 (.in(buffer_30_out));
  buf buffer_30 (buffer_30_out, or_14_out);
  or or_14 (or_14_out, rom_4_data[3], in_11);

  // Notes on the sheet:
  //   clock
  //   IPC INC
  //   Resetr
  //   IPC (counter)
  //   OUT
  //   IPC HIGH
  //   LOAD_CMD
  //   contents of CONTROL_ROM (hex, n*v repeats v):
  //   20 8 82 13*0 20 8 82 13*0 20 8 82 13*0 20 8 82 13*0 20 8 82 13*0 20 8 82 13*0 20 8 82 13*0 20 8 82
  //   13*0 20 8 82 13*0 20 8 82 13*0 20 8 82 13*0 20 8 82 13*0 20 8 82 13*0 20 8 82 13*0 20 8 82 13*0 20 8
  //   82 13*0 20 8 82 13*0 20 8 82 13*0 20 8 82 13*0 20 8 82 13*0 20 8 82 13*0 20 8 82 13*0 20 8 82 13*0
  //   20 8 82 13*0 20 8 82 13*0 20 8 82 13*0 20 8 82 13*0 20 8 82 13*0 20 8 82 13*0 20 8 82 13*0 20 8 82
  //   13*0 20 8 82 13*0 20 8 82 13*0 20 8 82 20 8 82 20 8 82 0 0 1 4*0 20 8 82 20 8 82 20 8 82 0 0 2 4*0
  //   20 8 82 20 8 2 80 9*0 20 8 82 20 8 2 80 9*0 20 8 82 20 8 2 80 9*0 20 8 82 20 8 2 80 9*0 20 8 82 20 8
  //   42 80 9*0 20 8 82 13*0 20 8 82 13*0 20 8 82 13*0 20 8 82 13*0 20 8 82 13*0 20 8 82 13*0 20 8 82 13*0
  //   20 8 82 13*0 20 8 82 13*0 20 8 82 13*0 20 8 82 13*0 20 8 82 13*0 20 8 82 13*0 20 8 82 13*0 20 8 82
  //   13*0 20 8 82 13*0 20 8 82 13*0 20 8 82 13*0 20 8 82 13*0 20 8 82 13*0 20 8 82 13*0 20 8 82 13*0 20 8
  //   82 13*0 20 8 82 13*0 20 8 82 20 8 82 20 8 12 4 6*0 20 8 82 80 80 11*0 20 8 82 80 80 11*0 20 8 82
  //   13*0 20 8 82 80 80 11*0 20 8 82 13*0 20 8 82 13*0 20 8 82 13*0 20 8 82 13*0 20 8 82 13*0 20 8 82
  //   13*0 20 8 82 13*0 20 8 82 13*0 20 8 82 13*0 20 8 82 13*0 20 8 82 13*0 20 8 82 13*0 20 8 82 80 80
  //   11*0 20 8 82 80 80 11*0 20 8 82 13*0 20 8 82 80 80 11*0 20 8 82 13*0 20 8 82 13*0 20 8 82 13*0 20 8
  //   82 13*0 20 8 82 13*0 20 8 82 13*0 20 8 82 13*0 20 8 82 13*0 20 8 82 13*0 20 8 82 13*0 20 8 82 13*0
  //   20 8 82 20 8 11*0 20 8 82 20 8 11*0 20 8 82 10 4 11*0 20 8 82 13*0 20 8 82 10 4 11*0 20 8 82 13*0 20
  //   8 82 13*0 20 8 82 13*0 20 8 82 13*0 20 8 82 13*0 20 8 82 13*0 20 8 82 13*0 20 8 82 13*0 20 8 82 13*0
  //   20 8 82 13*0 20 8 82 13*0 20 8 82 13*0 20 8 82 13*0 20 8 82 13*0 20 8 82 13*0 20 8 82 13*0 20 8 82
  //   13*0 20 8 82 13*0 20 8 82 13*0 20 8 82 13*0 20 8 82 13*0 20 8 82 13*0 20 8 82 13*0 20 8 82 13*0 20 8
  //   82 13*0 20 8 82 13*0 20 8 82 13*0 20 8 82 13*0 20 8 82 13*0 20 8 82 13*0 20 8 82 13*0 20 8 82 13*0
  //   20 8 82 13*0 20 8 82 13*0 20 8 82 13*0 20 8 82 13*0 20 8 82 13*0 20 8 82 13*0 20 8 82 13*0 20 8 82
  //   13*0 20 8 82 13*0 20 8 82 13*0 20 8 82 13*0 20 8 82 13*0 20 8 82 13*0 20 8 82 13*0 20 8 82 13*0 20 8
  //   82 13*0 20 8 82 13*0 20 8 82 13*0 20 8 82 13*0 20 8 82 13*0 20 8 82 13*0 20 8 82 13*0 20 8 82 13*0
  //   20 8 82 13*0 20 8 82 13*0 20 8 82 13*0 20 8 82 13*0 20 8 82 13*0 20 8 82 13*0 20 8 82 13*0 20 8 82
  //   13*0 20 8 82 13*0 20 8 82 13*0 20 8 82 13*0 20 8 82 13*0 20 8 82 13*0 20 8 82 13*0 20 8 82 13*0 20 8
  //   82 13*0 20 8 82 13*0 20 8 82 13*0 20 8 82 13*0 20 8 82 13*0 20 8 82 13*0 20 8 82 13*0 20 8 82 13*0
  //   20 8 82 13*0 20 8 82 13*0 20 8 82 13*0 20 8 82 13*0 20 8 82 13*0 20 8 82 13*0 20 8 82 13*0 20 8 82
  //   13*0 20 8 82 13*0 20 8 82 13*0 20 8 82 13*0 20 8 82 13*0 20 8 82 13*0 20 8 82 13*0 20 8 82 1 12*0 20
  //   8 82 4 12*0 20 8 82 10 12*0 20 8 82 13*0 20 8 82 13*0 20 8 82 13*0 20 8 82 13*0 20 8 82 40 12*0 20 8
  //   82 13*0 20 8 82 1 12*0 20 8 82 4 12*0 20 8 82 10 12*0 20 8 82 13*0 20 8 82 13*0 20 8 82 13*0 20 8 82
  //   13*0 20 8 82 40 12*0 20 8 82 2 12*0 20 8 82 2 12*0 20 8 82 6 12*0 20 8 82 12 12*0 20 8 82 2 12*0 20
  //   8 82 2 12*0 20 8 82 2 12*0 20 8 82 2 12*0 20 8 82 42 12*0 20 8 82 8 12*0 20 8 82 20 12*0 20 8 82 8
  //   12*0 20 8 82 20 12*0 20 8 82 9 12*0 20 8 82 21 12*0 20 8 82 13*0 20 8 82 13*0 20 8 82 13*0 20 8 82
  //   13*0 20 8 82 1 12*0 20 8 82 1 12*0 20 8 82 13*0 20 8 82 13*0 20 8 82 13*0 20 8 82 13*0 20 8 82 1
  //   12*0 20 8 82 1 12*0 20 8 82 13*0 20 8 82 13*0 20 8 82 1 12*0 20 8 82 4 12*0 20 8 82 10 12*0 20 8 82
  //   13*0 20 8 82 13*0 20 8 82 13*0 20 8 82 13*0 20 8 82 40 12*0 20 8 82 13*0 20 8 82 13*0 20 8 82 13*0
  //   20 8 82 13*0 20 8 82 13*0 20 8 82 13*0 20 8 82 13*0 20 8 82 13*0 20 8 82
  //   IPC LOW
  //   MEM
  //   A
  //   contents of rom_1 (hex, n*v repeats v):
  //   0 0 2 13*1 0 0 2 1 0 11*1 0 0 2 1 0 11*1 0 0 2 1 0 11*1 0 0 2 1 0 11*1 0 0 2 13*1 0 0 2 13*1 0 0 2
  //   13*1 0 0 2 1 0 11*1 0 0 2 1 0 11*1 0 0 2 1 0 11*1 0 0 2 1 0 11*1 0 0 2 1 0 11*1 0 0 2 13*1 0 0 2
  //   13*1 0 0 2 13*1 0 0 2 13*1 0 0 2 13*1 0 0 2 13*1 0 0 2 13*1 0 0 2 13*1 0 0 2 13*1 0 0 2 13*1 0 0 2
  //   13*1 0 0 2 13*1 0 0 2 13*1 0 0 2 13*1 0 0 2 13*1 0 0 2 13*1 0 0 2 13*1 0 0 2 13*1 0 0 2 13*1 0 0 2
  //   13*1 0 0 2 8*0 81 4*1 0 0 2 8*0 41 4*1 0 0 2 0 0 40 10*1 0 0 2 0 0 10 10*1 0 0 2 0 0 0 10*1 0 0 2 0
  //   0 0 10*1 0 0 2 0 0 0 10*1 0 0 2 13*1 0 0 2 13*1 0 0 2 13*1 0 0 2 13*1 0 0 2 13*1 0 0 2 13*1 0 0 2
  //   13*1 0 0 2 13*1 0 0 2 13*1 0 0 2 13*1 0 0 2 13*1 0 0 2 13*1 0 0 2 13*1 0 0 2 13*1 0 0 2 13*1 0 0 2
  //   13*1 0 0 2 13*1 0 0 2 13*1 0 0 2 13*1 0 0 2 13*1 0 0 2 13*1 0 0 2 13*1 0 0 2 13*1 0 0 2 13*1 0 0 2
  //   6*0 7*1 0 0 2 0 12*1 0 0 2 0 12*1 0 0 2 13*1 0 0 2 0 12*1 0 0 2 13*1 0 0 2 13*1 0 0 2 13*1 0 0 2
  //   13*1 0 0 2 13*1 0 0 2 13*1 0 0 2 13*1 0 0 2 13*1 0 0 2 13*1 0 0 2 13*1 0 0 2 13*1 0 0 2 13*1 0 0 2 0
  //   12*1 0 0 2 0 12*1 0 0 2 13*1 0 0 2 0 12*1 0 0 2 13*1 0 0 2 13*1 0 0 2 13*1 0 0 2 13*1 0 0 2 13*1 0 0
  //   2 13*1 0 0 2 13*1 0 0 2 13*1 0 0 2 13*1 0 0 2 13*1 0 0 2 13*1 0 0 2 0 0 11*1 0 0 2 0 0 11*1 0 0 2 0
  //   0 11*1 0 0 2 0 0 11*1 0 0 2 0 0 11*1 0 0 2 0 0 11*1 0 0 2 13*1 0 0 2 13*1 0 0 2 13*1 0 0 2 13*1 0 0
  //   2 13*1 0 0 2 13*1 0 0 2 13*1 0 0 2 13*1 0 0 2 13*1 0 0 2 13*1 0 0 2 13*1 0 0 2 13*1 0 0 2 13*1 0 0 2
  //   13*1 0 0 2 13*1 0 0 2 13*1 0 0 2 13*1 0 0 2 13*1 0 0 2 13*1 0 0 2 13*1 0 0 2 13*1 0 0 2 13*1 0 0 2
  //   13*1 0 0 2 13*1 0 0 2 13*1 0 0 2 13*1 0 0 2 13*1 0 0 2 13*1 0 0 2 13*1 0 0 2 13*1 0 0 2 13*1 0 0 2
  //   13*1 0 0 2 13*1 0 0 2 13*1 0 0 2 13*1 0 0 2 13*1 0 0 2 13*1 0 0 2 13*1 0 0 2 13*1 0 0 2 13*1 0 0 2
  //   13*1 0 0 2 13*1 0 0 2 13*1 0 0 2 13*1 0 0 2 13*1 0 0 2 13*1 0 0 2 13*1 0 0 2 13*1 0 0 2 13*1 0 0 2
  //   13*1 0 0 2 13*1 0 0 2 13*1 0 0 2 13*1 0 0 2 13*1 0 0 2 13*1 0 0 2 13*1 0 0 2 13*1 0 0 2 13*1 0 0 2
  //   13*1 0 0 2 13*1 0 0 2 13*1 0 0 2 13*1 0 0 2 13*1 0 0 2 13*1 0 0 2 13*1 0 0 2 13*1 0 0 2 13*1 0 0 2
  //   13*1 0 0 2 13*1 0 0 2 13*1 0 0 2 13*1 0 0 2 13*1 0 0 2 13*1 0 0 2 13*1 0 0 2 13*1 0 0 2 13*1 0 0 2
  //   13*1 0 0 2 13*1 0 0 2 13*1 0 0 2 13*1 0 0 2 13*1 0 0 2 13*1 0 0 2 13*1 0 0 2 13*1 0 0 2 13*1 0 0 2
  //   13*1 0 0 2 13*1 0 0 2 13*1 0 0 2 13*1 0 0 2 13*1 0 0 2 91 12*1 0 0 2 81 12*1 0 0 2 81 12*1 0 0 2 81
  //   12*1 0 0 2 81 12*1 0 0 2 81 12*1 0 0 2 81 12*1 0 0 2 81 12*1 0 0 2 81 12*1 0 0 2 61 12*1 0 0 2 21
  //   12*1 0 0 2 21 12*1 0 0 2 21 12*1 0 0 2 21 12*1 0 0 2 21 12*1 0 0 2 21 12*1 0 0 2 21 12*1 0 0 2 21
  //   12*1 0 0 2 41 12*1 0 0 2 11 12*1 0 0 2 13*1 0 0 2 13*1 0 0 2 13*1 0 0 2 13*1 0 0 2 13*1 0 0 2 13*1 0
  //   0 2 13*1 0 0 2 41 12*1 0 0 2 41 12*1 0 0 2 11 12*1 0 0 2 11 12*1 0 0 2 13*1 0 0 2 13*1 0 0 2 41 12*1
  //   0 0 2 41 12*1 0 0 2 11 12*1 0 0 2 11 12*1 0 0 2 13*1 0 0 2 13*1 0 0 2 41 12*1 0 0 2 41 12*1 0 0 2 11
  //   12*1 0 0 2 11 12*1 0 0 2 13*1 0 0 2 13*1 0 0 2 41 12*1 0 0 2 11 12*1 0 0 2 13*1 0 0 2 13*1 0 0 2
  //   13*1 0 0 2 13*1 0 0 2 13*1 0 0 2 13*1 0 0 2 13*1 0 0 2 13*1 0 0 2 13*1 0 0 2 13*1 0 0 2 13*1 0 0 2
  //   13*1 0 0 2 13*1 0 0 2 13*1 0 0 2 13*1 0 0 2 13*1 0 0 2 0 12*1
  //   END_CMD
  //   B
  //   contents of rom_2 (hex, n*v repeats v):
  //   40 10 14*0 40 10 14*0 40 10 14*0 40 10 14*0 40 10 14*0 40 10 14*0 40 10 14*0 40 10 14*0 40 10 14*0
  //   40 10 14*0 40 10 14*0 40 10 14*0 40 10 14*0 40 10 14*0 40 10 14*0 40 10 14*0 40 10 14*0 40 10 14*0
  //   40 10 14*0 40 10 14*0 40 10 14*0 40 10 14*0 40 10 14*0 40 10 14*0 40 10 14*0 40 10 14*0 40 10 14*0
  //   40 10 14*0 40 10 14*0 40 10 14*0 40 10 14*0 40 10 14*0 40 10 14*0 40 10 0 40 10 1 40 10 4 12 48 5*0
  //   40 10 0 40 10 1 40 10 4 12 48 5*0 40 10 0 40 10 11*0 40 10 0 40 10 11*0 40 10 0 40 10 4 10*0 40 10 0
  //   40 10 1 10*0 40 10 0 40 10 11*0 40 10 14*0 40 10 14*0 40 10 14*0 40 10 14*0 40 10 14*0 40 10 14*0 40
  //   10 14*0 40 10 14*0 40 10 14*0 40 10 14*0 40 10 14*0 40 10 14*0 40 10 14*0 40 10 14*0 40 10 14*0 40
  //   10 14*0 40 10 14*0 40 10 14*0 40 10 14*0 40 10 14*0 40 10 14*0 40 10 14*0 40 10 14*0 40 10 14*0 40
  //   10 0 40 10 1 40 10 0 2 6*0 40 10 14*0 40 10 14*0 40 10 14*0 40 10 14*0 40 10 14*0 40 10 14*0 40 10
  //   14*0 40 10 14*0 40 10 14*0 40 10 14*0 40 10 14*0 40 10 14*0 40 10 14*0 40 10 14*0 40 10 14*0 40 10
  //   14*0 40 10 14*0 40 10 14*0 40 10 14*0 40 10 14*0 40 10 14*0 40 10 14*0 40 10 14*0 40 10 14*0 40 10
  //   14*0 40 10 14*0 40 10 14*0 40 10 14*0 40 10 14*0 40 10 14*0 40 10 14*0 40 10 0 40 10 11*0 40 10 0 4
  //   1 11*0 40 10 0 80 20 11*0 40 10 0 84 21 11*0 40 10 0 8 2 11*0 40 10 0 48 12 11*0 40 10 14*0 40 10
  //   14*0 40 10 14*0 40 10 14*0 40 10 14*0 40 10 14*0 40 10 14*0 40 10 14*0 40 10 14*0 40 10 14*0 40 10
  //   14*0 40 10 14*0 40 10 14*0 40 10 14*0 40 10 14*0 40 10 14*0 40 10 14*0 40 10 14*0 40 10 14*0 40 10
  //   14*0 40 10 14*0 40 10 14*0 40 10 14*0 40 10 14*0 40 10 14*0 40 10 14*0 40 10 14*0 40 10 14*0 40 10
  //   14*0 40 10 14*0 40 10 14*0 40 10 14*0 40 10 14*0 40 10 14*0 40 10 14*0 40 10 14*0 40 10 14*0 40 10
  //   14*0 40 10 14*0 40 10 14*0 40 10 14*0 40 10 14*0 40 10 14*0 40 10 14*0 40 10 14*0 40 10 14*0 40 10
  //   14*0 40 10 14*0 40 10 14*0 40 10 14*0 40 10 14*0 40 10 14*0 40 10 14*0 40 10 14*0 40 10 14*0 40 10
  //   14*0 40 10 14*0 40 10 14*0 40 10 14*0 40 10 14*0 40 10 14*0 40 10 14*0 40 10 14*0 40 10 14*0 40 10
  //   14*0 40 10 14*0 40 10 14*0 40 10 14*0 40 10 14*0 40 10 14*0 40 10 14*0 40 10 14*0 40 10 14*0 40 10
  //   14*0 40 10 14*0 40 10 14*0 40 10 14*0 40 10 14*0 40 10 14*0 40 10 14*0 40 10 14*0 40 10 14*0 40 10
  //   14*0 40 10 14*0 40 10 14*0 40 10 14*0 40 10 14*0 40 10 14*0 40 10 14*0 40 10 14*0 40 10 14*0 40 10
  //   14*0 40 10 14*0 40 10 14*0 40 10 0 10 12*0 40 10 0 40 12*0 40 10 0 1 12*0 40 10 0 4 12*0 40 10 14*0
  //   40 10 14*0 40 10 14*0 40 10 14*0 40 10 14*0 40 10 0 10 12*0 40 10 0 40 12*0 40 10 0 1 12*0 40 10 0 4
  //   12*0 40 10 14*0 40 10 14*0 40 10 14*0 40 10 14*0 40 10 14*0 40 10 0 10 12*0 40 10 0 40 12*0 40 10 0
  //   1 12*0 40 10 0 4 12*0 40 10 14*0 40 10 14*0 40 10 14*0 40 10 14*0 40 10 14*0 40 10 14*0 40 10 14*0
  //   40 10 0 20 12*0 40 10 0 80 12*0 40 10 0 20 12*0 40 10 0 80 12*0 40 10 0 20 12*0 40 10 0 80 12*0 40
  //   10 0 2 12*0 40 10 0 8 12*0 40 10 0 2 12*0 40 10 0 8 12*0 40 10 0 2 12*0 40 10 0 8 12*0 40 10 14*0 40
  //   10 14*0 40 10 14*0 40 10 14*0 40 10 14*0 40 10 0 10 12*0 40 10 0 40 12*0 40 10 0 1 12*0 40 10 0 4
  //   12*0 40 10 14*0 40 10 14*0 40 10 14*0 40 10 14*0 40 10 14*0 40 10 14*0 40 10 14*0 40 10 14*0 40 10
  //   14*0 40 10
  //   MR_HIGH
  //   MR_LOW
  //   TR_HIGH
  //   TR_LOW
  //   M
  //   contents of rom_3 (hex, n*v repeats v):
  //   35*0 f 15*0 c 15*0 10 63*0 9 15*0 6 15*0 1b 15*0 16 15*0 1
  //   S3
  //   S2
  //   BUS
  //   S0
  //   S1
  //   BUS_WR
  //   contents of rom_4 (hex, n*v repeats v):
  //   19*0 64 15*0 54 15*0 44 15*0 54 15*0 20 15*0 10 15*0 10 15*0 44 15*0 64 15*0 54 15*0 44 15*0 44
  //   3599*0 80 15*0 80 15*0 80 15*0 80 15*0 80 15*0 80 15*0 80 15*0 80 15*0 80 15*0 80 143*0 8
  //   ALU
  //   set
  //   Clear
  //   Carry IN
  //   HALT
endmodule
