// Logisim project control_v6.circ as structural Verilog: 1 circuit, main circuit main
module main (
  input  in_1,
  input  in_2,
  input  Carry,
  input  EQUAL,
  input  SPARE,
  input  in_6,
  input  in_7,
  input  in_8,
  input  in_9,
  input  in_10,
  input  in_11,
  input  in_12,
  input  in_13
);

  wire and_1_out, and_2_out, and_3_out, and_4_out, and_5_out, and_6_out, and_7_out, and_8_out, and_9_out,
       and_10_out, and_11_out, and_12_out, and_18_out, and_19_out, and_20_out, and_21_out, and_22_out,
       and_23_out, and_24_out, and_26_out, and_27_out, and_28_out, and_29_out, and_30_out, buffer_1_out,
       buffer_2_out, buffer_3_out, buffer_4_out, buffer_5_out, buffer_6_out, buffer_7_out, buffer_8_out,
       buffer_9_out, buffer_10_out, buffer_11_out, button_1_out, button_2_out, button_3_out, button_4_out,
       decoder_1_out1, decoder_1_out2, decoder_1_out3, decoder_2_out1, decoder_2_out2, decoder_2_out3,
       decoder_2_out4, decoder_2_out5, decoder_2_out6, decoder_2_out7, decoder_3_out1, decoder_3_out2,
       decoder_3_out3, decoder_3_out4, decoder_3_out5, decoder_3_out6, decoder_3_out7, decoder_4_out0,
       decoder_4_out1, decoder_4_out2, decoder_4_out3, decoder_5_out1, decoder_5_out2, decoder_5_out3,
       decoder_5_out4, decoder_5_out5, decoder_5_out6, decoder_5_out7, decoder_6_out2, decoder_6_out3,
       decoder_6_out4, decoder_6_out5, decoder_6_out6, decoder_6_out7, j_k_ff_1_qn, j_k_ff_2_q, nand_1_out,
       nand_2_out, nand_3_out, nand_4_out, nand_5_out, nand_6_out, not_1_out, not_2_out, not_3_out,
       not_4_out, not_5_out, not_6_out, not_7_out, not_8_out, not_9_out, not_10_out, not_11_out, not_12_out,
       not_13_out, not_14_out, not_15_out, not_16_out, or_1_out, or_2_out, or_3_out, or_4_out, or_5_out,
       or_6_out, or_7_out, or_8_out, or_9_out, or_10_out, or_15_out, or_16_out, or_17_out, or_20_out,
       or_23_out, or_24_out, or_25_out, or_26_out, or_27_out, or_28_out, xor_1_out;
  wire [2:0] or_19_out;
  wire [2:2] counter_2_q;
  wire [3:0] dipswitch_1_sw4;
  wire [7:0] CODE_data, CONTROL_ROM_data, counter_1_q, counter_2_q_2, or_21_out, register_1_q;

  and and_1 (and_1_out, in_2, decoder_3_out2);
  and and_2 (and_2_out, in_1, decoder_6_out2);
  and and_3 (and_3_out, button_1_out, or_1_out);
  or or_1 (or_1_out, and_1_out, and_2_out, and_27_out, decoder_1_out3);
  DipSwitch #(.number(4)) dipswitch_1 (
    .sw1(dipswitch_1_sw4[3]), .sw2(dipswitch_1_sw4[2]), .sw3(dipswitch_1_sw4[1]), .sw4(dipswitch_1_sw4[0]));
  Button button_1 (.out(button_1_out));
  Button button_2 (.out(button_2_out));
  LED led_1 (.in(and_3_out));
  not not_1 (not_1_out, button_1_out);
  LED led_2 (.in(button_1_out));
  LED led_3 (.in(button_2_out));
  Counter counter_1 (.clr(button_2_out), .clk(and_3_out), .Q(counter_1_q));  // open: load, up, count, D, carry
  Counter #(.width(4), .max('hf)) counter_2 (
    .clr(button_2_out), .load(or_2_out), .clk(not_1_out), .D(dipswitch_1_sw4),
    .Q({counter_2_q_2[2], counter_2_q[2], counter_2_q_2[1:0]}));  // open: up, count, carry
  or or_2 (or_2_out, and_6_out, and_29_out);
  ROM CODE (.addr(counter_1_q), .data(CODE_data));
  LED led_4 (.in(counter_2_q[2]));
  LED led_5 (.in(counter_2_q_2[0]));
  LED led_6 (.in(counter_2_q_2[1]));
  LED led_7 (.in(counter_2_q_2[2]));
  not not_2 (not_2_out, register_1_q[5]);
  not not_3 (not_3_out, register_1_q[7]);
  and and_4 (and_4_out, not_3_out, not_2_out);
  and and_5 (and_5_out, register_1_q[6], and_4_out);
  LED led_8 (.in(and_5_out));
  Decoder #(.select(4), .enable("false")) decoder_1 (
    .out1(decoder_1_out1), .out2(decoder_1_out2), .out3(decoder_1_out3),
    .sel({counter_2_q_2[2], counter_2_q[2], counter_2_q_2[1:0]}));  // open: out0, out4, out5, out6, out7, out8, out9, out10, out11, out12, out13, out14, out15
  and and_6 (and_6_out, and_7_out, counter_2_q[2]);
  xor xor_1 (xor_1_out, register_1_q[4], or_3_out);
  or or_3 (or_3_out, or_5_out, or_6_out);
  and and_7 (and_7_out, register_1_q[6], register_1_q[7]);
  or or_4 (or_4_out, counter_2_q_2[2], counter_2_q[2]);
  and and_8 (and_8_out, xor_1_out, and_5_out);
  not not_4 (not_4_out, and_8_out);
  and and_9 (and_9_out, register_1_q[0], j_k_ff_1_qn);
  or or_5 (or_5_out, and_9_out, and_10_out);
  and and_10 (and_10_out, register_1_q[1], Carry);
  and and_11 (and_11_out, register_1_q[2], and_18_out);
  or or_6 (or_6_out, and_11_out, and_12_out);
  and and_12 (and_12_out, register_1_q[3], SPARE);
  Register register_1 (.D(CODE_data), .en(decoder_1_out3), .clk(button_1_out), .Q(register_1_q), .clr(button_2_out));
  and and_13 (counter_2_q_2[3], register_1_q[0], not_4_out);
  and and_14 (counter_2_q_2[4], register_1_q[1], not_4_out);
  and and_15 (counter_2_q_2[5], register_1_q[2], not_4_out);
  and and_16 (counter_2_q_2[6], register_1_q[3], not_4_out);
  and and_17 (counter_2_q_2[7], register_1_q[4], not_4_out);
  LED led_9 (.in(j_k_ff_1_qn));
  and and_18 (and_18_out, EQUAL, EQUAL);
  LED led_10 (.in(not_5_out));
  LED led_11 (.in(nand_1_out));
  nand nand_1 (nand_1_out, button_1_out, decoder_3_out1);
  not not_5 (not_5_out, or_7_out);
  or or_7 (or_7_out, decoder_2_out1, decoder_5_out1);
  LED led_12 (.in(or_8_out));
  or or_8 (or_8_out, and_6_out, register_1_q[0], register_1_q[1], register_1_q[2], register_1_q[3], register_1_q[4], register_1_q[5], register_1_q[6], register_1_q[7]);
  ROM #(.addrWidth(11)) CONTROL_ROM (.addr({register_1_q[7:5], counter_2_q_2}), .data(CONTROL_ROM_data));
  LED led_13 (.in(buffer_1_out));
  buf buffer_1 (buffer_1_out, or_9_out);
  or or_9 (or_9_out, decoder_1_out2, decoder_2_out2);
  not not_6 (not_6_out, or_8_out);
  LED led_14 (.in(not_7_out));
  LED led_15 (.in(not_8_out));
  not not_7 (not_7_out, decoder_2_out4);
  not not_8 (not_8_out, decoder_2_out3);
  J_K_Flip_Flop j_k_ff_1 (.J(or_8_out), .K(not_6_out), .clk(button_1_out), .Qn(j_k_ff_1_qn));  // open: Q, preset, reset
  LED led_16 (.in(buffer_2_out));
  LED led_17 (.in(nand_2_out));
  nand nand_2 (nand_2_out, button_1_out, or_10_out);
  buf buffer_2 (buffer_2_out, decoder_3_out2);
  or or_10 (or_10_out, decoder_3_out3, decoder_1_out2);
  Decoder #(.select(3)) decoder_2 (
    .out1(decoder_2_out1), .out2(decoder_2_out2), .out3(decoder_2_out3), .out4(decoder_2_out4),
    .out5(decoder_2_out5), .out6(decoder_2_out6), .out7(decoder_2_out7), .sel(or_19_out), .en(decoder_4_out1));  // open: out0
  or or_11 (or_21_out[6], CONTROL_ROM_data[6], in_7);
  or or_12 (or_21_out[7], CONTROL_ROM_data[7], in_6);
  LED led_18 (.in(nand_3_out));
  nand nand_3 (nand_3_out, button_1_out, decoder_3_out4);
  Decoder #(.select(3)) decoder_3 (
    .out1(decoder_3_out1), .out2(decoder_3_out2), .out3(decoder_3_out3), .out4(decoder_3_out4),
    .out5(decoder_3_out5), .out6(decoder_3_out6), .out7(decoder_3_out7), .sel(or_21_out[7:5]),
    .en(decoder_4_out1));  // open: out0
  or or_13 (or_21_out[5], CONTROL_ROM_data[5], in_8);
  or or_14 (or_19_out[2], CONTROL_ROM_data[4], in_9);
  LED led_19 (.in(not_9_out));
  LED led_20 (.in(not_10_out));
  not not_9 (not_9_out, or_15_out);
  not not_10 (not_10_out, or_16_out);
  or or_15 (or_15_out, decoder_2_out5, decoder_5_out5);
  or or_16 (or_16_out, decoder_3_out5, decoder_6_out5);
  Decoder #(.select(2)) decoder_4 (
    .out0(decoder_4_out0), .out1(decoder_4_out1), .out2(decoder_4_out2), .out3(decoder_4_out3),
    .sel(or_21_out[1:0]), .en(or_17_out));
  or or_17 (or_17_out, or_4_out, button_4_out);
  or or_18 (or_19_out[1], CONTROL_ROM_data[3], in_10);
  or or_19 (or_19_out[0], CONTROL_ROM_data[2], in_11);
  LED led_21 (.in(not_11_out));
  not not_11 (not_11_out, or_20_out);
  or or_20 (or_20_out, decoder_2_out6, decoder_5_out6);
  Decoder #(.select(3)) decoder_5 (
    .out1(decoder_5_out1), .out2(decoder_5_out2), .out3(decoder_5_out3), .out4(decoder_5_out4),
    .out5(decoder_5_out5), .out6(decoder_5_out6), .out7(decoder_5_out7), .sel(or_19_out), .en(decoder_4_out2));  // open: out0
  or or_21 (or_21_out[0], CONTROL_ROM_data[0], in_13);
  or or_22 (or_21_out[1], CONTROL_ROM_data[1], in_12);
  LED led_22 (.in(not_12_out));
  not not_12 (not_12_out, or_23_out);
  or or_23 (or_23_out, decoder_3_out6, decoder_6_out6);
  Button button_3 (.out(button_3_out));
  LED led_23 (.in(buffer_3_out));
  LED led_24 (.in(and_19_out));
  and and_19 (and_19_out, button_1_out, or_25_out);
  buf buffer_3 (buffer_3_out, or_24_out);
  or or_24 (or_24_out, decoder_2_out7, decoder_5_out7);
  or or_25 (or_25_out, decoder_3_out7, decoder_6_out7);
  Decoder #(.select(3)) decoder_6 (
    .out2(decoder_6_out2), .out3(decoder_6_out3), .out4(decoder_6_out4), .out5(decoder_6_out5),
    .out6(decoder_6_out6), .out7(decoder_6_out7), .sel(or_21_out[7:5]), .en(decoder_4_out2));  // open: out0, out1
  Button button_4 (.out(button_4_out));
  LED led_25 (.in(buffer_4_out));
  buf buffer_4 (buffer_4_out, or_26_out);
  or or_26 (or_26_out, decoder_1_out1, decoder_5_out2);
  and and_20 (and_20_out, or_19_out[0], decoder_4_out3);
  and and_21 (and_21_out, or_19_out[1], decoder_4_out3);
  and and_22 (and_22_out, or_19_out[2], decoder_4_out3);
  and and_23 (and_23_out, or_21_out[5], decoder_4_out3);
  and and_24 (and_24_out, or_21_out[6], decoder_4_out3);
  // AND_Gate and_25 has open pins: in0=or_21_out[7], in1=decoder_4_out3, out=open
  LED led_26 (.in(not_13_out));
  LED led_27 (.in(not_14_out));
  not not_13 (not_13_out, decoder_5_out4);
  not not_14 (not_14_out, decoder_5_out3);
  and and_26 (and_26_out, or_19_out[0], decoder_4_out0);
  and and_27 (and_27_out, or_19_out[2], decoder_4_out0);
  and and_28 (and_28_out, or_21_out[6], decoder_4_out0);
  LED led_28 (.in(buffer_5_out));
  buf buffer_5 (buffer_5_out, decoder_6_out2);
  and and_29 (and_29_out, or_19_out[1], decoder_4_out0);
  and and_30 (and_30_out, or_21_out[5], decoder_4_out0);
  // AND_Gate and_31 has open pins: in0=or_21_out[7], in1=decoder_4_out0, out=open
  LED led_29 (.in(nand_4_out));
  LED led_30 (.in(nand_5_out));
  nand nand_4 (nand_4_out, button_1_out, or_27_out);
  nand nand_5 (nand_5_out, button_1_out, decoder_6_out4);
  or or_27 (or_27_out, decoder_6_out3, decoder_1_out1);
  LED led_31 (.in(nand_6_out));
  nand nand_6 (nand_6_out, button_1_out, decoder_4_out3);
  LED led_32 (.in(buffer_7_out));
  LED led_33 (.in(buffer_6_out));
  buf buffer_6 (buffer_6_out, and_21_out);
  buf buffer_7 (buffer_7_out, and_20_out);
  LED led_34 (.in(buffer_8_out));
  buf buffer_8 (buffer_8_out, and_22_out);
  LED led_35 (.in(buffer_9_out));
  LED led_36 (.in(buffer_10_out));
  buf buffer_9 (buffer_9_out, and_23_out);
  buf buffer_10 (buffer_10_out, and_24_out);
  LED led_37 (.in(and_30_out));
  not not_15 (not_15_out, not_16_out);
  LED led_38 (.in(and_28_out));
  not not_16 (not_16_out, and_28_out);
  LED led_39 (.in(j_k_ff_2_q));
  J_K_Flip_Flop j_k_ff_2 (
    .J(and_30_out), .K(not_15_out), .clk(button_1_out), .Q(j_k_ff_2_q));  // open: Qn, preset, reset
  or or_28 (or_28_out, and_26_out, button_3_out);
  LED led_40 (.in(buffer_11_out));
  buf buffer_11 (buffer_11_out, or_28_out);

  // Notes on the sheet:
  //   Dummy AND gates
  //   nur fuer Simulation
  //   IPC reagiert auf load korrekt
  //   IPC clock
  //   clock
  //   Resetr
  //   IPC (counter)
  //   contents of CODE (hex, n*v repeats v):
  //   0 1 2 3 4 5 6 6 7 8 9 a b c 21 45 75 22 45 75 23 55 24 55 25 55 26 55 27 55 40 45 75 41 45 75 42 45
  //   75 43 45 75 44 45 75 45 45 75 46 45 75 41 45 75 42 45 75 43 45 75 44 45 75 45 45 75 46 45 75 60 61
  //   62 63 64 65 c0 c1 c2 c3 c4 c5 c6 c7 c8 c9 ca cb cc cd ce cf d0 d1 d2 d3 d4 d5 d6 d7 d8 d9 da db dc
  //   dd de df e0 e1 e2 e3 e4 e5 e6 e7 e8 e9 ea eb ec ed ee ef f0 f1 f2 f3 f4 f5 f6 ff
  //   ALU
  //   OUT
  //   use 9 diodes
  //   +inverter
  //   contents of CONTROL_ROM (hex, n*v repeats v):
  //   8*8 3 28 6*8 7b 7*8 1b 7*8 7 7*8 28 7*8 28 7*8 48 7*8 4b 7*8 33 28 6*8 6f 7*8 37 7*8 43 167*8 89 10
  //   6a 71 f5 18 8 8 89 10 6a 71 bd 18 8 8 6a 69 bd 18 4*8 6a 69 dd 18 4*8 6a 69 9d 18 4*8 6a 69 9d 18
  //   4*8 6a 69 3d 18 196*8 9d 10 5e 51 4*8 9d 10 5e 51 5*8 10 5e 51 4*8 9d 10 5e 51 5*8 10 5e 51 4*8 9d
  //   10 5e 51 5*8 10 5e 51 204*8 69 6a 6*8 89 8a 6*8 4d 4e 6*8 8d 8e 6*8 51 52 6*8 71 72 726*8 d5 7*8 f5
  //   7*8 55 7*8 56 7*8 75 7*8 76 7*8 95 7*8 96 7*8 35 7*8 b9 7*8 f9 7*8 59 7*8 5a 7*8 79 7*8 7a 7*8 99
  //   7*8 9a 7*8 39 7*8 bd 7*8 dd 7*8 5d 7*8 5e 7*8 7d 7*8 7e 7*8 9d 7*8 9e 7*8 3d 7*8 a9 7*8 aa 7*8 c9
  //   7*8 ca 7*8 e9 7*8 ea 7*8 ad 7*8 ae 7*8 cd 7*8 ce 7*8 ed 7*8 ee 7*8 b1 7*8 b2 7*8 d1 7*8 d2 7*8 f1
  //   7*8 f2 7*8 a5 7*8 c5 7*8 e5 7*8 45 7*8 46 7*8 65 7*8 66 7*8 85 7*8 86 7*8 25 71*8 4 7*8
  //   Zero
  //   IPC
  //   LOW
  //   TMR
  //   MR
  //   MR
  //   IPC
  //   SRC LOW
  //   TMR
  //   A
  //   TAR LOW
  //   B
  //   SRC HIGH
  //   manual halt
  //   MEM
  //   IPC
  //   TAR HIGH
  //   manual enable selector for step4+
  //   TMR
  //   MR
  //   74LS237; LE/OE1 constant low; OE0 for enable
  //   IPC
  //   HIGH
  //   MR
  //   TMR
  //   ENA
  //   M
  //   S3
  //   ALU
  //   S2
  //   S1
  //   S0
  //   set
  //   Clear
  //   Carry IN
  //   HALT
endmodule
